// Logisim project Circuit_Diagram.circ as structural Verilog: 6 circuits, main circuit main
module main (
  input  [31:0] A,
  input  [31:0] B,
  output [63:0] out_val
);
endmodule

module shift_left (
  input  [31:0] in_value_2,
  output [31:0] shift_result,
  output carry_out
);


  assign carry_out = in_value_2[0];
  assign shift_result = {1'b0, in_value_2[31:1]};
endmodule

module shift_right (
  input  [31:0] in_value_2,
  output [31:0] shift_result,
  output carry_out
);


  assign carry_out = in_value_2[31];
  assign shift_result = {in_value_2[30:0], 1'b0};
endmodule

module fac_1b (
  input  c_in,
  input  x,
  input  y,
  output z,
  output c_out
);

  wire and_1_out, and_2_out, and_3_out, xor_2_out;

  or or_1 (c_out, and_1_out, and_2_out, and_3_out);
  and and_1 (and_1_out, c_in, x);
  and and_2 (and_2_out, c_in, y);
  and and_3 (and_3_out, y, x);
  xor xor_1 (z, xor_2_out, c_in);
  xor xor_2 (xor_2_out, x, y);
endmodule

module sum_32b (
  input  pad_to_64,
  input  c_in,
  input  [31:0] in_x,
  input  [31:0] in_y,
  output [63:0] out_val
);

  wire fac_1b_1_c_out, fac_1b_2_c_out, fac_1b_3_c_out, fac_1b_4_c_out, fac_1b_5_c_out, fac_1b_6_c_out,
       fac_1b_7_c_out, fac_1b_8_c_out, fac_1b_9_c_out, fac_1b_10_c_out, fac_1b_11_c_out, fac_1b_12_c_out,
       fac_1b_13_c_out, fac_1b_14_c_out, fac_1b_15_c_out, fac_1b_16_c_out, fac_1b_17_c_out, fac_1b_18_c_out,
       fac_1b_19_c_out, fac_1b_20_c_out, fac_1b_21_c_out, fac_1b_22_c_out, fac_1b_23_c_out, fac_1b_24_c_out,
       fac_1b_25_c_out, fac_1b_26_c_out, fac_1b_27_c_out, fac_1b_28_c_out, fac_1b_29_c_out, fac_1b_30_c_out,
       fac_1b_31_c_out, fac_1b_32_c_out;

  fac_1b fac_1b_1 (.c_in(fac_1b_2_c_out), .x(in_x[31]), .y(in_y[31]), .z(out_val[31]), .c_out(fac_1b_1_c_out));
  fac_1b fac_1b_2 (.c_in(fac_1b_3_c_out), .x(in_x[30]), .y(in_y[30]), .z(out_val[30]), .c_out(fac_1b_2_c_out));
  fac_1b fac_1b_3 (.c_in(fac_1b_4_c_out), .x(in_x[29]), .y(in_y[29]), .z(out_val[29]), .c_out(fac_1b_3_c_out));
  fac_1b fac_1b_4 (.c_in(fac_1b_5_c_out), .x(in_x[28]), .y(in_y[28]), .z(out_val[28]), .c_out(fac_1b_4_c_out));
  fac_1b fac_1b_5 (.c_in(fac_1b_6_c_out), .x(in_x[27]), .y(in_y[27]), .z(out_val[27]), .c_out(fac_1b_5_c_out));
  fac_1b fac_1b_6 (.c_in(fac_1b_7_c_out), .x(in_x[26]), .y(in_y[26]), .z(out_val[26]), .c_out(fac_1b_6_c_out));
  fac_1b fac_1b_7 (.c_in(fac_1b_8_c_out), .x(in_x[25]), .y(in_y[25]), .z(out_val[25]), .c_out(fac_1b_7_c_out));
  fac_1b fac_1b_8 (.c_in(fac_1b_9_c_out), .x(in_x[24]), .y(in_y[24]), .z(out_val[24]), .c_out(fac_1b_8_c_out));
  fac_1b fac_1b_9 (.c_in(fac_1b_10_c_out), .x(in_x[23]), .y(in_y[23]), .z(out_val[23]), .c_out(fac_1b_9_c_out));
  fac_1b fac_1b_10 (.c_in(fac_1b_11_c_out), .x(in_x[22]), .y(in_y[22]), .z(out_val[22]), .c_out(fac_1b_10_c_out));
  fac_1b fac_1b_11 (.c_in(fac_1b_12_c_out), .x(in_x[21]), .y(in_y[21]), .z(out_val[21]), .c_out(fac_1b_11_c_out));
  fac_1b fac_1b_12 (.c_in(fac_1b_13_c_out), .x(in_x[20]), .y(in_y[20]), .z(out_val[20]), .c_out(fac_1b_12_c_out));
  fac_1b fac_1b_13 (.c_in(fac_1b_14_c_out), .x(in_x[19]), .y(in_y[19]), .z(out_val[19]), .c_out(fac_1b_13_c_out));
  fac_1b fac_1b_14 (.c_in(fac_1b_15_c_out), .x(in_x[18]), .y(in_y[18]), .z(out_val[18]), .c_out(fac_1b_14_c_out));
  fac_1b fac_1b_15 (.c_in(fac_1b_16_c_out), .x(in_x[17]), .y(in_y[17]), .z(out_val[17]), .c_out(fac_1b_15_c_out));
  fac_1b fac_1b_16 (.c_in(fac_1b_17_c_out), .x(in_x[16]), .y(in_y[16]), .z(out_val[16]), .c_out(fac_1b_16_c_out));
  fac_1b fac_1b_17 (.c_in(fac_1b_18_c_out), .x(in_x[15]), .y(in_y[15]), .z(out_val[15]), .c_out(fac_1b_17_c_out));
  fac_1b fac_1b_18 (.c_in(fac_1b_19_c_out), .x(in_x[14]), .y(in_y[14]), .z(out_val[14]), .c_out(fac_1b_18_c_out));
  fac_1b fac_1b_19 (.c_in(fac_1b_20_c_out), .x(in_x[13]), .y(in_y[13]), .z(out_val[13]), .c_out(fac_1b_19_c_out));
  fac_1b fac_1b_20 (.c_in(fac_1b_21_c_out), .x(in_x[12]), .y(in_y[12]), .z(out_val[12]), .c_out(fac_1b_20_c_out));
  fac_1b fac_1b_21 (.c_in(fac_1b_22_c_out), .x(in_x[11]), .y(in_y[11]), .z(out_val[11]), .c_out(fac_1b_21_c_out));
  fac_1b fac_1b_22 (.c_in(fac_1b_23_c_out), .x(in_x[10]), .y(in_y[10]), .z(out_val[10]), .c_out(fac_1b_22_c_out));
  fac_1b fac_1b_23 (.c_in(fac_1b_24_c_out), .x(in_x[9]), .y(in_y[9]), .z(out_val[9]), .c_out(fac_1b_23_c_out));
  fac_1b fac_1b_24 (.c_in(fac_1b_25_c_out), .x(in_x[8]), .y(in_y[8]), .z(out_val[8]), .c_out(fac_1b_24_c_out));
  fac_1b fac_1b_25 (.c_in(fac_1b_26_c_out), .x(in_x[7]), .y(in_y[7]), .z(out_val[7]), .c_out(fac_1b_25_c_out));
  fac_1b fac_1b_26 (.c_in(fac_1b_27_c_out), .x(in_x[6]), .y(in_y[6]), .z(out_val[6]), .c_out(fac_1b_26_c_out));
  fac_1b fac_1b_27 (.c_in(fac_1b_28_c_out), .x(in_x[5]), .y(in_y[5]), .z(out_val[5]), .c_out(fac_1b_27_c_out));
  or or_1 (out_val[32], pad_to_64, fac_1b_1_c_out);
  fac_1b fac_1b_28 (.c_in(fac_1b_29_c_out), .x(in_x[4]), .y(in_y[4]), .z(out_val[4]), .c_out(fac_1b_28_c_out));
  fac_1b fac_1b_29 (.c_in(fac_1b_30_c_out), .x(in_x[3]), .y(in_y[3]), .z(out_val[3]), .c_out(fac_1b_29_c_out));
  fac_1b fac_1b_30 (.c_in(fac_1b_31_c_out), .x(in_x[2]), .y(in_y[2]), .z(out_val[2]), .c_out(fac_1b_30_c_out));
  fac_1b fac_1b_31 (.c_in(fac_1b_32_c_out), .x(in_x[1]), .y(in_y[1]), .z(out_val[1]), .c_out(fac_1b_31_c_out));
  fac_1b fac_1b_32 (.c_in(c_in), .x(in_x[0]), .y(in_y[0]), .z(out_val[0]), .c_out(fac_1b_32_c_out));

  assign out_val[63:33] = {31{pad_to_64}};
endmodule

module sub_32b (
  input  [31:0] in_1,
  input  [31:0] in_2,
  output [63:0] out_val
);

  wire [31:0] not_1_out;

  assign not_1_out = ~in_2;  // NOT_Gate not_1, 32 bits wide
  sum_32b sum_32b_1 (.c_in(1'b1), .in_x(in_1), .in_y(not_1_out), .out_val(out_val));  // open: pad_to_64
endmodule
